# Fritzing sketch Device 1 (saved by Fritzing 0.9.3b)

parts:
  U4 = NodeMCU V3.0
  DHT1 = DHT11 Humitidy and Temperature Sensor
  R1 = Resistor [tolerance=±5% resistance=4.7k package=THT]  # not connected

nets:
  N1: U4.D0, DHT1.DATA
  3V3: U4.3V3, DHT1.VDD
  GND: U4.GND, DHT1.GND

custom parts:
  NodeMCU V3.0: ESP8266 based NodeMCU
  DHT11 Humitidy and Temperature Sensor: DHT11 Humidity and Temperature Sensor
