# Fritzing sketch Device 2 (saved by Fritzing 0.9.3b)

parts:
  U4 = NodeMCU V3.0
  KY-1 = Keyes Relay [package=THT]

nets:
  N1: U4.D0, KY-1.signal
  N2: U4.GND, KY-1.ground
  N3: U4.Vin, KY-1.power

custom parts:
  NodeMCU V3.0: ESP8266 based NodeMCU
  Keyes Relay: The Keyes 5V relay module is suitable for SCM development, home appliance control. It uses a 5V~12V TIL control signal which can control DC / AC signal.
