# Fritzing sketch Device 4 (saved by Fritzing 0.9.3b)

parts:
  U4 = NodeMCU V3.0
  hc-sr1 = hc-sr04

nets:
  N1: U4.D0, hc-sr1.Trig
  N2: U4.D1, hc-sr1.Echo
  GND: U4.GND, hc-sr1.GND
  VIN: U4.Vin, hc-sr1.VCC

custom parts:
  NodeMCU V3.0: ESP8266 based NodeMCU
