# Fritzing sketch Device 5 (saved by Fritzing 0.9.3b)

parts:
  U4 = NodeMCU V3.0
  Part1 = NeoPixel NeoMatrix 8x8 [part_number=1487]

nets:
  N1: U4.D0, Part1.IN
  N2: U4.GND, Part1.OUT
  VIN: U4.Vin, Part1.GND

custom parts:
  NodeMCU V3.0: ESP8266 based NodeMCU
  NeoPixel NeoMatrix 8x8: Put on your sunglasses before wiring up this LED matrix - 64 eye-blistering RGB LEDs adorn the NeoMatrix for a blast of configurable color. Arranged in an 8x8 matrix, each pixel is individually addressable. Only one microcontroller pin is required to control all the LEDs, and you get 24 bit color for each LED.
